# Fritzing sketch FingerPrintDoorLock_Fritzing.Ver03 (saved by Fritzing 1.0.2b)
breadboards: 1

parts:
  Sensor1 = TTP223B Capacitive Touch Sensor Module
  부품1 = sensor_biometrico
  부품2 = Arduino Uno (Rev3) - ICSP
  SERVO1 = Tower Pro SG90 servo [part_number=101246]

nets:
  GND: Sensor1.GND, 부품1.GND, 부품2.GND, SERVO1.GND
  VCC: Sensor1.VCC, 부품2.5V, SERVO1.+5V
  N1: Sensor1.SIG, 부품2.D2
  N2: 부품1.VCC, 부품2.D8
  N3: 부품1.TX, 부품2.D4
  N4: 부품1.RX, 부품2.D3_PWM
  N5: 부품2.D9_PWM, SERVO1.Signal

custom parts:
  TTP223B Capacitive Touch Sensor Module: The TTP223B capacitive touch sensor module uses the TTP223B IC. The appropriate voltage is approximately 2 to 5.5 volts.
  sensor_biometrico: Adafruit Optical Fingerprint Sensor
  Tower Pro SG90 servo: Original file by John De Cristofaro http://www.adafruit.com/products/1449 Adafruit Feedback Servo (Small) Edited by: e-radionica.com 28/9/2015
